// Logisim project alu.circ as structural Verilog: 18 circuits, main circuit alu
module alu (
  input  [31:0] A,
  input  [31:0] B,
  input  [3:0] ALUSel,
  output [31:0] Result
);

  classifier classifier_1 (.A(A), .B(B), .Sel(ALUSel), .Res(Result));

  // Notes on the sheet:
  //   INPUTS to your circuit
  //   DON'T CHANGE THE LOCATIONS OF THE INPUTS AND OUTPUTS!
  //   OUTPUT from your circuit
endmodule

module classifier (
  input  [31:0] A,
  input  [31:0] B,
  input  [3:0] Sel,
  output [31:0] Res
);

  wire [31:0] AddRes, AndRes, BitpalRes, CntoRes, DivuRes, MulhRes, MultRes, OrRes, RemuRes, SirRes, SllRes,
       SltRes, SraRes, SrlRes, SubRes, XorRes;

  add add_1 (.A(A), .B(B), .Res(AddRes));
  sub sub_1 (.A(A), .B(B), .Res(SubRes));
  mulh mulh_1 (.A(A), .B(B), .Res(MulhRes));
  mult mult_1 (.A(A), .B(B), .Res(MultRes));
  divu divu_1 (.A(A), .B(B), .Res(DivuRes));
  remu remu_1 (.A(A), .B(B), .Res(RemuRes));
  mand mand_1 (.A(A), .B(B), .Res(AndRes));
  mor mor_1 (.A(A), .B(B), .Res(OrRes));
  mxor mxor_1 (.A(A), .B(B), .Res(XorRes));
  msll msll_1 (.A(A), .B(B), .Res(SllRes));
  slt slt_1 (.A(A), .B(B), .Res(SltRes));
  msra msra_1 (.A(A), .B(B), .Res(SraRes));
  msrl msrl_1 (.A(A), .B(B), .Res(SrlRes));
  cnto cnto_1 (.A(A), .B(B), .Res(CntoRes));
  bitpal bitpal_1 (.A(A), .B(B), .Res(BitpalRes));
  sir sir_1 (.A(A), .B(B), .Res(SirRes));
  Multiplexer #(.select(4), .width(32), .enable("false")) multiplexer_1 (
    .in0(AddRes), .in1(SubRes), .in2(MulhRes), .in3(MultRes), .in4(DivuRes), .in5(RemuRes), .in6(AndRes),
    .in7(OrRes), .in8(XorRes), .in9(SllRes), .in10(SltRes), .in11(SraRes), .in12(SrlRes), .in13(CntoRes),
    .in14(BitpalRes), .in15(SirRes), .out(Res), .sel(Sel));
endmodule

module add (
  input  [31:0] A,
  input  [31:0] B,
  output [31:0] Res
);

  Adder #(.width(32)) adder_1 (.a(A), .b(B), .out(Res));  // open: cin, cout
endmodule

module sub (
  input  [31:0] A,
  input  [31:0] B,
  output [31:0] Res
);

  Subtractor #(.width(32)) subtractor_1 (.a(A), .b(B), .out(Res));  // open: bin, bout
endmodule

module mulh (
  input  [31:0] A,
  input  [31:0] B,
  output [31:0] Res
);

  wire adder_3_cout;
  wire [31:0] adder_1_out, ALow, Aupper, bit_extender_5_out, bit_extender_6_out, BLow, Bupper,
       multiplier_1_out, multiplier_2_out, multiplier_3_out, multiplier_4_out, shifter_1_out;

  Multiplier #(.width(32)) multiplier_1 (.a(Aupper), .b(Bupper), .out(multiplier_1_out));  // open: cin, cout
  Multiplier #(.width(32)) multiplier_2 (.a(Aupper), .b(BLow), .out(multiplier_2_out));  // open: cin, cout
  Multiplier #(.width(32)) multiplier_3 (.a(ALow), .b(Bupper), .out(multiplier_3_out));  // open: cin, cout
  Multiplier #(.width(32)) multiplier_4 (.a(ALow), .b(BLow), .out(multiplier_4_out));  // open: cin, cout
  assign Aupper = {{16{1'b0}}, A[15:0]};  // Bit_Extender bit_extender_1
  assign ALow = {{16{A[31]}}, A[31:16]};  // Bit_Extender bit_extender_2
  assign Bupper = {{16{1'b0}}, B[15:0]};  // Bit_Extender bit_extender_3
  assign BLow = {{16{B[31]}}, B[31:16]};  // Bit_Extender bit_extender_4
  Adder #(.width(32)) adder_1 (.a(multiplier_2_out), .b(multiplier_3_out), .out(adder_1_out));  // open: cin, cout
  assign bit_extender_5_out = {{16{1'b0}}, adder_1_out[15:0]};  // Bit_Extender bit_extender_5
  assign bit_extender_6_out = {{16{adder_1_out[31]}}, adder_1_out[31:16]};  // Bit_Extender bit_extender_6
  Shifter #(.width(32)) shifter_1 (.in(bit_extender_5_out), .\dist (5'b10000), .out(shifter_1_out));
  Adder #(.width(32)) adder_2 (
    .a(bit_extender_6_out), .b(multiplier_4_out), .out(Res), .cin(adder_3_cout));  // open: cout
  Adder #(.width(32)) adder_3 (.a(multiplier_1_out), .b(shifter_1_out), .cout(adder_3_cout));  // open: out, cin
endmodule

module mult (
  input  [31:0] A,
  input  [31:0] B,
  output [31:0] Res
);

  Multiplier #(.width(32)) multiplier_1 (.a(A), .b(B), .out(Res));  // open: cin, cout
endmodule

module divu (
  input  [31:0] A,
  input  [31:0] B,
  output [31:0] Res
);

  Divider #(.width(32)) divider_1 (.a(A), .b(B), .out(Res));  // open: upper, rem
endmodule

module remu (
  input  [31:0] A,
  input  [31:0] B,
  output [31:0] Res
);

  Divider #(.width(32)) divider_1 (.a(A), .b(B), .rem(Res));  // open: out, upper
endmodule

module mand (
  input  [31:0] A,
  input  [31:0] B,
  output [31:0] Res
);

  assign Res = A & B;  // AND_Gate and_1, 32 bits wide
endmodule

module mor (
  input  [31:0] A,
  input  [31:0] B,
  output [31:0] Res
);

  assign Res = A | B;  // OR_Gate or_1, 32 bits wide
endmodule

module mxor (
  input  [31:0] A,
  input  [31:0] B,
  output [31:0] Res
);

  assign Res = A ^ B;  // XOR_Gate xor_1, 32 bits wide
endmodule

module msll (
  input  [31:0] A,
  input  [31:0] B,
  output [31:0] Res
);

  Shifter #(.width(32)) shifter_1 (.in(A), .\dist (B[4:0]), .out(Res));
endmodule

module slt (
  input  [31:0] A,
  input  [31:0] B,
  output [31:0] Res
);

  wire comparator_1_lt;

  Comparator #(.width(32)) comparator_1 (.a(A), .b(B), .lt(comparator_1_lt));  // open: gt, eq
  assign Res = {{31{1'b0}}, comparator_1_lt};  // Bit_Extender bit_extender_1
endmodule

module msra (
  input  [31:0] A,
  input  [31:0] B,
  output [31:0] Res
);

  Shifter #(.width(32), .shift("ar")) shifter_1 (.in(A), .\dist (B[4:0]), .out(Res));
endmodule

module msrl (
  input  [31:0] A,
  input  [31:0] B,
  output [31:0] Res
);

  Shifter #(.width(32), .shift("lr")) shifter_1 (.in(A), .\dist (B[4:0]), .out(Res));
endmodule

module cnto (
  input  [31:0] A,
  input  [31:0] B,
  output [31:0] Res
);

  wire [6:0] bitadder_1_out;

  BitAdder #(.width(32)) bitadder_1 (.in0(A), .in1(B), .out(bitadder_1_out));
  assign Res = {{25{1'b0}}, bitadder_1_out};  // Bit_Extender bit_extender_1
endmodule

module bitpal (
  input  [31:0] A,
  input  [31:0] B,
  output [31:0] Res
);

  wire comparator_1_eq, comparator_2_eq;
  wire [31:0] bit_extender_1_out, bit_extender_2_out;

  Comparator #(.width(16)) comparator_1 (
    .a({A[0], A[1], A[2], A[3], A[4], A[5], A[6], A[7], A[8], A[9], A[10], A[11], A[12], A[13], A[14], A[15]}),
    .b(A[31:16]), .eq(comparator_1_eq));  // open: gt, lt
  Comparator #(.width(16)) comparator_2 (
    .a({B[0], B[1], B[2], B[3], B[4], B[5], B[6], B[7], B[8], B[9], B[10], B[11], B[12], B[13], B[14], B[15]}),
    .b(B[31:16]), .eq(comparator_2_eq));  // open: gt, lt
  assign bit_extender_1_out = {{31{1'b0}}, comparator_1_eq};  // Bit_Extender bit_extender_1
  assign bit_extender_2_out = {{31{1'b0}}, comparator_2_eq};  // Bit_Extender bit_extender_2
  assign Res = bit_extender_1_out | bit_extender_2_out;  // OR_Gate or_1, 32 bits wide
endmodule

module sir (
  input  [31:0] A,
  input  [31:0] B,
  output [31:0] Res
);

  wire comparator_1_eq;

  assign Res = {{31{1'b0}}, comparator_1_eq};  // Bit_Extender bit_extender_1
  Comparator #(.width(32)) comparator_1 (
    .a(A),
    .b({B[0], B[1], B[2], B[3], B[4], B[5], B[6], B[7], B[8], B[9], B[10], B[11], B[12], B[13], B[14], B[15], B[16], B[17], B[18], B[19], B[20], B[21], B[22], B[23], B[24], B[25], B[26], B[27], B[28], B[29], B[30], B[31]}),
    .eq(comparator_1_eq));  // open: gt, lt
endmodule
