// Logisim project alu.circ as structural Verilog: 1 circuit, main circuit alu
module alu (
  input  [31:0] A,
  input  [31:0] B,
  input  [3:0] ALUSel,
  output [31:0] Result
);

  wire comparator_1_eq, comparator_2_lt, comparator_3_lt;
  wire [1:0] signBA;
  wire [4:0] bit_extender_2_out, bit_extender_3_out, bit_extender_4_out;
  wire [31:0] Add, adder_2_out, and_1_out, and_2_out, divider_1_out, divider_1_rem, Divu, Mulh, MulhNn,
       MulhNp, MulhPn, Mulhu, Mult, multiplier_2_cout, multiplier_3_cout, multiplier_4_cout, my_And, my_Or,
       my_sll, my_sra, my_srl, my_Xor, Remu, shifter_1_out, shifter_2_out, slti, sltu, Sub, subtractor_4_out;

  Divider #(.width(32)) divider_1 (.a(A), .b(B), .out(divider_1_out), .rem(divider_1_rem));  // open: upper
  Comparator #(.width(32)) comparator_1 (.a(B), .b({32{1'b0}}), .eq(comparator_1_eq));  // open: gt, lt
  Multiplier #(.width(32)) multiplier_1 (.a(A), .b(B), .out(Mult), .cout(Mulhu));  // open: cin
  Multiplier #(.width(32)) multiplier_2 (.a(A), .b(B), .cout(multiplier_2_cout));  // open: out, cin
  Multiplier #(.width(32)) multiplier_3 (.a(A), .b(B), .cout(multiplier_3_cout));  // open: out, cin
  Multiplier #(.width(32)) multiplier_4 (.a(A), .b(B), .cout(multiplier_4_cout));  // open: out, cin
  assign and_1_out = 32'h80000000 & A;  // AND_Gate and_1, 32 bits wide
  assign and_2_out = B & 32'h80000000;  // AND_Gate and_2, 32 bits wide
  Adder #(.width(32)) adder_1 (.a(A), .b(B), .out(Add));  // open: cin, cout
  Subtractor #(.width(32)) subtractor_1 (.a(A), .b(B), .out(Sub));  // open: bin, bout
  Multiplexer #(.width(32), .enable("false")) multiplexer_1 (
    .in0(divider_1_rem), .in1(A), .out(Remu), .sel(comparator_1_eq));
  Subtractor #(.width(32)) subtractor_2 (.a(multiplier_2_cout), .b(B), .out(MulhNp));  // open: bin, bout
  Subtractor #(.width(32)) subtractor_3 (.a(multiplier_3_cout), .b(A), .out(MulhPn));  // open: bin, bout
  Subtractor #(.width(32)) subtractor_4 (.a(multiplier_4_cout), .b(A), .out(subtractor_4_out));  // open: bin, bout
  Shifter #(.width(32), .shift("lr")) shifter_1 (.in(and_1_out), .\dist ({5{1'b1}}), .out(shifter_1_out));
  Shifter #(.width(32), .shift("lr")) shifter_2 (.in(and_2_out), .\dist (5'b11110), .out(shifter_2_out));
  Multiplexer #(.select(2), .width(32), .enable("false")) multiplexer_2 (
    .in0(Mulhu), .in1(MulhNp), .in2(MulhPn), .in3(MulhNn), .out(Mulh), .sel(signBA));
  Subtractor #(.width(32)) subtractor_5 (.a(subtractor_4_out), .b(B), .out(MulhNn));  // open: bin, bout
  Adder #(.width(32)) adder_2 (.a(shifter_1_out), .b(shifter_2_out), .out(adder_2_out));  // open: cin, cout
  Bit_Extender #(.in_width(32), .out_width(2), .\type ("zero")) bit_extender_1 (.in(adder_2_out), .out(signBA));
  Multiplexer #(.width(32), .enable("false")) multiplexer_3 (
    .in0(divider_1_out), .in1(A), .out(Divu), .sel(comparator_1_eq));
  Bit_Extender #(.in_width(32), .out_width(5)) bit_extender_2 (.in(B), .out(bit_extender_2_out));
  Bit_Extender #(.in_width(32), .out_width(5)) bit_extender_3 (.in(B), .out(bit_extender_3_out));
  Bit_Extender #(.in_width(32), .out_width(5)) bit_extender_4 (.in(B), .out(bit_extender_4_out));
  Comparator #(.width(32)) comparator_2 (.a(A), .b(B), .lt(comparator_2_lt));  // open: gt, eq
  Comparator #(.width(32), .mode("unsigned")) comparator_3 (.a(A), .b(B), .lt(comparator_3_lt));  // open: gt, eq
  assign my_And = A & B;  // AND_Gate and_3, 32 bits wide
  assign my_Or = A | B;  // OR_Gate or_1, 32 bits wide
  assign my_Xor = A ^ B;  // XOR_Gate xor_1, 32 bits wide
  Shifter #(.width(32), .shift("lr")) shifter_3 (.in(A), .\dist (bit_extender_2_out), .out(my_srl));
  Shifter #(.width(32), .shift("ar")) shifter_4 (.in(A), .\dist (bit_extender_3_out), .out(my_sra));
  Shifter #(.width(32)) shifter_5 (.in(A), .\dist (bit_extender_4_out), .out(my_sll));
  assign sltu = {{31{1'b0}}, comparator_2_lt};  // Bit_Extender bit_extender_5
  assign slti = {{31{1'b0}}, comparator_3_lt};  // Bit_Extender bit_extender_6
  Multiplexer #(.select(4), .width(32), .enable("false")) multiplexer_4 (
    .in0(my_And), .in1(my_Or), .in2(my_Xor), .in3(Add), .in4(Sub), .in5(Mult), .in6(Mulhu), .in7(Mulh),
    .in8(Divu), .in9(Remu), .in10(my_srl), .in11(my_sra), .in12(my_sll), .in13(sltu), .in14(slti),
    .out(Result), .sel(ALUSel));  // open: in15

  // Notes on the sheet:
  //   INPUTS to your circuit
  //   DON'T CHANGE THE LOCATIONS OF THE INPUTS AND OUTPUTS!
  //   OUTPUT from your circuit
endmodule
