// Logisim project alu.circ as structural Verilog: 1 circuit, main circuit alu
module alu (
  input  [31:0] A,
  input  [31:0] B,
  input  [3:0] ALUSel,
  output [31:0] Result
);

  wire comparator_1_eq, comparator_2_lt, comparator_3_gt;
  wire [1:0] bit_extender_1_out;
  wire [4:0] bit_extender_2_out, bit_extender_3_out, bit_extender_4_out;
  wire [6:0] bitadder_1_out;
  wire [31:0] Add, adder_2_out, and_1_out, and_2_out, cnto, divider_1_out, divider_1_rem, Divu, Mulh, Mulhu,
       Mult, my_And, my_Or, my_sll, my_sra, my_srl, my_Xor, Remu, shifter_1_out, shifter_2_out, sir, slt,
       Sub, subtractor_1_out, subtractor_2_out, subtractor_3_out;

  Divider #(.width(32)) divider_1 (.a(A), .b(B), .out(divider_1_out), .rem(divider_1_rem));  // open: upper
  Comparator #(.width(32)) comparator_1 (.a(B), .b({32{1'b0}}), .eq(comparator_1_eq));  // open: gt, lt
  Multiplier #(.width(32)) multiplier_1 (.a(A), .b(B), .out(Mult), .cout(Mulhu));  // open: cin
  Subtractor #(.width(32)) subtractor_1 (.a(Mulhu), .b(B), .out(subtractor_1_out));  // open: bin, bout
  Subtractor #(.width(32)) subtractor_2 (.a(Mulhu), .b(A), .out(subtractor_2_out));  // open: bin, bout
  Subtractor #(.width(32)) subtractor_3 (.a(subtractor_2_out), .b(B), .out(subtractor_3_out));  // open: bin, bout
  Adder #(.width(32)) adder_1 (.a(A), .b(B), .out(Add));  // open: cin, cout
  Subtractor #(.width(32)) subtractor_4 (.a(A), .b(B), .out(Sub));  // open: bin, bout
  Multiplexer #(.width(32), .enable("false")) multiplexer_1 (
    .in0(divider_1_rem), .in1(A), .out(Remu), .sel(comparator_1_eq));
  assign and_1_out = 32'h80000000 & A;  // AND_Gate and_1, 32 bits wide
  assign and_2_out = B & 32'h80000000;  // AND_Gate and_2, 32 bits wide
  Shifter #(.width(32), .shift("lr")) shifter_1 (.in(and_1_out), .\dist ({5{1'b1}}), .out(shifter_1_out));
  Adder #(.width(32)) adder_2 (.a(shifter_1_out), .b(shifter_2_out), .out(adder_2_out));  // open: cin, cout
  Shifter #(.width(32), .shift("lr")) shifter_2 (.in(and_2_out), .\dist (5'b11110), .out(shifter_2_out));
  Multiplexer #(.width(32), .enable("false")) multiplexer_2 (
    .in0(divider_1_out), .in1(A), .out(Divu), .sel(comparator_1_eq));
  Multiplexer #(.select(2), .width(32), .enable("false")) multiplexer_3 (
    .in0(Mulhu), .in1(subtractor_1_out), .in2(subtractor_2_out), .in3(subtractor_3_out), .out(Mulh),
    .sel(bit_extender_1_out));
  Bit_Extender #(.in_width(32), .out_width(2), .\type ("zero")) bit_extender_1 (
    .in(adder_2_out), .out(bit_extender_1_out));
  Bit_Extender #(.in_width(32), .out_width(5)) bit_extender_2 (.in(B), .out(bit_extender_2_out));
  Bit_Extender #(.in_width(32), .out_width(5)) bit_extender_3 (.in(B), .out(bit_extender_3_out));
  Bit_Extender #(.in_width(32), .out_width(5)) bit_extender_4 (.in(B), .out(bit_extender_4_out));
  Comparator #(.width(32)) comparator_2 (.a(A), .b(B), .lt(comparator_2_lt));  // open: gt, eq
  BitAdder #(.width(32)) bitadder_1 (.in0(A), .in1(B), .out(bitadder_1_out));
  assign my_And = A & B;  // AND_Gate and_3, 32 bits wide
  assign my_Or = A | B;  // OR_Gate or_1, 32 bits wide
  assign my_Xor = A ^ B;  // XOR_Gate xor_1, 32 bits wide
  Shifter #(.width(32), .shift("lr")) shifter_3 (.in(A), .\dist (bit_extender_2_out), .out(my_srl));
  Shifter #(.width(32), .shift("ar")) shifter_4 (.in(A), .\dist (bit_extender_3_out), .out(my_sra));
  Shifter #(.width(32)) shifter_5 (.in(A), .\dist (bit_extender_4_out), .out(my_sll));
  assign slt = {{31{1'b0}}, comparator_2_lt};  // Bit_Extender bit_extender_5
  assign cnto = {{25{1'b0}}, bitadder_1_out};  // Bit_Extender bit_extender_6
  assign sir = {{31{1'b0}}, comparator_3_gt};  // Bit_Extender bit_extender_7
  Comparator #(.width(32)) comparator_3 (
    .a(A),
    .b({B[0], B[1], B[2], B[3], B[4], B[5], B[6], B[7], B[8], B[9], B[10], B[11], B[12], B[13], B[14], B[15], B[16], B[17], B[18], B[19], B[20], B[21], B[22], B[23], B[24], B[25], B[26], B[27], B[28], B[29], B[30], B[31]}),
    .gt(comparator_3_gt));  // open: eq, lt
  Multiplexer #(.select(4), .width(32), .enable("false")) multiplexer_4 (
    .in0(my_And), .in1(my_Or), .in2(my_Xor), .in3(Add), .in4(Sub), .in5(Mult), .in6(Mulhu), .in7(Mulh),
    .in8(Divu), .in9(Remu), .in10(my_srl), .in11(my_sra), .in12(my_sll), .in13(slt), .in14(cnto), .in15(sir),
    .out(Result), .sel(ALUSel));

  // Notes on the sheet:
  //   INPUTS to your circuit
  //   DON'T CHANGE THE LOCATIONS OF THE INPUTS AND OUTPUTS!
  //   OUTPUT from your circuit
endmodule
