// Logisim project cpu.circ as structural Verilog: 6 circuits, main circuit main
module main (
  input  [31:0] INSTRUCTION,
  input  CLOCK,
  output [31:0] FETCH_ADDRESS,
  output [31:0] ra,
  output [31:0] sp,
  output [31:0] t0,
  output [31:0] t1,
  output [31:0] t2,
  output [31:0] s0,
  output [31:0] s1,
  output [31:0] a0
);

  wire ASel, BrEq, BrLt, BrUn, BSel, lbu, lh, lhu, lui, lw, MemRW, PCSel, RegWEn;
  wire [1:0] WBSel;
  wire [2:0] ImmSel;
  wire [3:0] ALUSel;
  wire [4:0] RR1, RR2, RW;
  wire [31:0] adder_1_out, adder_2_out, ALURes, DMEM_readdata, Imm, inst2ControlLogic,
       instructiondecode_1_inst_imm, memdata_1_my_output, multiplexer_1_out, multiplexer_2_out,
       multiplexer_3_out, multiplexer_4_out, multiplexer_5_out, PC_q, R2, RegFile_read_data_1, register_2_q,
       Res;

  Multiplexer #(.width(32), .enable("false")) multiplexer_1 (
    .in0(INSTRUCTION), .in1(32'h13), .out(multiplexer_1_out), .sel(PCSel));
  InstructionDecode instructiondecode_1 (
    .Instruction(inst2ControlLogic), .Inst24_20(RR2), .Inst19_15(RR1), .Inst11_7(RW),
    .Inst_imm(instructiondecode_1_inst_imm));
  Register #(.width(32)) register_1 (
    .D(multiplexer_1_out), .en(1'b1), .clk(CLOCK), .Q(inst2ControlLogic));  // open: clr
  ImmGenerator immgenerator_1 (.inst31_7(instructiondecode_1_inst_imm), .ImmSel(ImmSel), .imm(Imm));
  Adder #(.width(32)) adder_1 (.a(PC_q), .b(32'h4), .out(adder_1_out));  // open: cin, cout
  Multiplexer #(.width(32), .enable("false")) multiplexer_2 (
    .in0(adder_1_out), .in1(ALURes), .out(multiplexer_2_out), .sel(PCSel));
  ControlLogic controllogic_1 (
    .Instruction(inst2ControlLogic), .BrEq(BrEq), .BrLt(BrLt), .MemRW(MemRW), .lh(lh), .PCSel(PCSel),
    .lw(lw), .ASel(ASel), .RegWEn(RegWEn), .lbu(lbu), .BSel(BSel), .BrUn(BrUn), .lhu(lhu), .ImmSel(ImmSel),
    .lui(lui), .WBSel(WBSel), .ALUSel(ALUSel));
  Register #(.width(32)) PC (.D(multiplexer_2_out), .en(1'b1), .clk(CLOCK), .Q(PC_q));  // open: clr
  Register #(.width(32)) register_2 (.D(PC_q), .en(1'b1), .clk(CLOCK), .Q(register_2_q));  // open: clr
  Shifter #(.width(32), .shift("lr")) shifter_1 (.in(PC_q), .\dist (5'b00010), .out(FETCH_ADDRESS));
  regfile_main RegFile (
    .Read_Register_1_rs1(RR1), .Read_Register_2_rs2(RR2), .Write_Register_rd(RW), .Write_Data(Res),
    .Write_Enable(RegWEn), .Clock(CLOCK), .Read_Data_1(RegFile_read_data_1), .Read_Data_2(R2), .ra(ra),
    .sp(sp), .t0(t0), .t1(t1), .t2(t2), .s0(s0), .s1(s1), .a0(a0));
  Multiplexer #(.width(32), .enable("false")) multiplexer_3 (
    .in0(RegFile_read_data_1), .in1(register_2_q), .out(multiplexer_3_out), .sel(ASel));
  Multiplexer #(.width(32), .enable("false")) multiplexer_4 (.in0(R2), .in1(Imm), .out(multiplexer_4_out), .sel(BSel));
  Adder #(.width(32)) adder_2 (.a(register_2_q), .b(32'h4), .out(adder_2_out));  // open: cin, cout
  Multiplexer #(.width(32), .enable("false")) multiplexer_5 (
    .in0(multiplexer_3_out), .in1({32{1'b0}}), .out(multiplexer_5_out), .sel(lui));
  BranchCompare branchcompare_1 (.DataA(RegFile_read_data_1), .DataB(R2), .BrUn(BrUn), .BrEq(BrEq), .BrLt(BrLt));
  mem_main DMEM (.WriteAddr(ALURes), .MemRW(MemRW), .clk(CLOCK), .WriteData(R2), .ReadData(DMEM_readdata));
  alu Arithmetic_Logic_Unit (.A(multiplexer_5_out), .B(multiplexer_4_out), .ALUSel(ALUSel), .Result(ALURes));
  MemData memdata_1 (.ReadData(DMEM_readdata), .lh(lh), .lw(lw), .lbu(lbu), .lhu(lhu), .my_Output(memdata_1_my_output));
  Multiplexer #(.select(2), .width(32), .enable("false")) multiplexer_6 (
    .in0(memdata_1_my_output), .in1(ALURes), .in2(adder_2_out), .out(Res), .sel(WBSel));  // open: in3

  // Other names for the same wires on the sheet: clk = CLOCK; fetch_addr[31:0] = FETCH_ADDRESS

  // Notes on the sheet:
  //   Output
  //   Inputs/Outputs from run.circ. DO NOT MOVE THESE.
  //   Inputs
  //   Inputs/Outputs from run.circ. DO NOT MOVE THESE.
endmodule

module InstructionDecode (
  input  [31:0] Instruction,
  output [4:0] Inst24_20,
  output [4:0] Inst19_15,
  output [4:0] Inst11_7,
  output [31:0] Inst_imm
);

  wire [31:0] bit_extender_1_out;

  assign bit_extender_1_out = {{7{1'b0}}, Instruction[31:7]};  // Bit_Extender bit_extender_1
  Shifter #(.width(32)) shifter_1 (.in(bit_extender_1_out), .\dist (5'b00111), .out(Inst_imm));

  assign Inst11_7 = Instruction[11:7];
  assign Inst19_15 = Instruction[19:15];
  assign Inst24_20 = Instruction[24:20];
endmodule

module ImmGenerator (
  input  [31:0] inst31_7,
  input  [2:0] ImmSel,
  output [31:0] imm
);

  wire comparator_1_eq, comparator_2_eq, comparator_3_eq, comparator_4_eq, comparator_5_eq;
  wire [31:0] bit_extender_1_out, bit_extender_2_out, bit_extender_3_out, bit_extender_4_out;

  assign bit_extender_1_out = {{20{inst31_7[31]}}, inst31_7[31:20]};  // Bit_Extender bit_extender_1
  Comparator #(.width(3)) comparator_1 (.a(ImmSel), .b(3'b000), .eq(comparator_1_eq));  // open: gt, lt
  assign bit_extender_2_out = {{20{inst31_7[31]}}, {inst31_7[31:25], inst31_7[11:7]}};  // Bit_Extender bit_extender_2
  Comparator #(.width(3)) comparator_2 (.a(ImmSel), .b(3'b001), .eq(comparator_2_eq));  // open: gt, lt
  assign bit_extender_3_out = {{19{inst31_7[31]}}, {inst31_7[31], inst31_7[7], inst31_7[30:25], inst31_7[11:8], 1'b0}};  // Bit_Extender bit_extender_3
  Comparator #(.width(3)) comparator_3 (.a(ImmSel), .b(3'b010), .eq(comparator_3_eq));  // open: gt, lt
  assign bit_extender_4_out = {{19{inst31_7[31]}}, {inst31_7[31], inst31_7[20], inst31_7[30:21], 1'b0}};  // Bit_Extender bit_extender_4
  Comparator #(.width(3)) comparator_4 (.a(ImmSel), .b(3'b011), .eq(comparator_4_eq));  // open: gt, lt
  Comparator #(.width(3)) comparator_5 (.a(ImmSel), .b(3'b100), .eq(comparator_5_eq));  // open: gt, lt
  assign imm = comparator_1_eq ? bit_extender_1_out : 32'bz;  // Controlled_Buffer controlled_buffer_1
  assign imm = comparator_2_eq ? bit_extender_2_out : 32'bz;  // Controlled_Buffer controlled_buffer_2
  assign imm = comparator_3_eq ? bit_extender_3_out : 32'bz;  // Controlled_Buffer controlled_buffer_3
  assign imm = comparator_4_eq ? bit_extender_4_out : 32'bz;  // Controlled_Buffer controlled_buffer_4
  assign imm = comparator_5_eq ? {inst31_7[31:12], {12{1'b0}}} : 32'bz;  // Controlled_Buffer controlled_buffer_5

  // Other names for the same wires on the sheet: inst_imm[31:0] = inst31_7
endmodule

module BranchCompare (
  input  [31:0] DataA,
  input  [31:0] DataB,
  input  BrUn,
  output BrEq,
  output BrLt
);

  wire comparator_1_eq, comparator_1_lt, comparator_2_eq, comparator_2_lt, not_1_out;

  Comparator #(.width(32)) comparator_1 (.a(DataA), .b(DataB), .eq(comparator_1_eq), .lt(comparator_1_lt));  // open: gt
  Comparator #(.width(32), .mode("unsigned")) comparator_2 (
    .a(DataA), .b(DataB), .eq(comparator_2_eq), .lt(comparator_2_lt));  // open: gt
  assign BrEq = not_1_out ? comparator_1_eq : 1'bz;  // Controlled_Buffer controlled_buffer_1
  assign BrLt = not_1_out ? comparator_1_lt : 1'bz;  // Controlled_Buffer controlled_buffer_2
  assign BrEq = BrUn ? comparator_2_eq : 1'bz;  // Controlled_Buffer controlled_buffer_3
  assign BrLt = BrUn ? comparator_2_lt : 1'bz;  // Controlled_Buffer controlled_buffer_4
  not not_1 (not_1_out, BrUn);

  // Other names for the same wires on the sheet: InputA[31:0] = DataA; InputB[31:0] = DataB
endmodule

module MemData (
  input  [31:0] ReadData,
  input  lh,
  input  lw,
  input  lbu,
  input  lhu,
  output [31:0] my_Output
);

  wire [31:0] bit_extender_1_out, bit_extender_2_out, bit_extender_3_out, bit_extender_4_out,
       multiplexer_1_out, multiplexer_2_out, multiplexer_3_out;

  assign bit_extender_1_out = {{24{1'b0}}, ReadData[7:0]};  // Bit_Extender bit_extender_1
  assign bit_extender_2_out = {{24{ReadData[7]}}, ReadData[7:0]};  // Bit_Extender bit_extender_2
  assign bit_extender_3_out = {{16{ReadData[15]}}, ReadData[15:0]};  // Bit_Extender bit_extender_3
  assign bit_extender_4_out = {{16{1'b0}}, ReadData[15:0]};  // Bit_Extender bit_extender_4
  Multiplexer #(.width(32), .enable("false")) multiplexer_1 (
    .in0(bit_extender_2_out), .in1(bit_extender_3_out), .out(multiplexer_1_out), .sel(lh));
  Multiplexer #(.width(32), .enable("false")) multiplexer_2 (
    .in0(multiplexer_1_out), .in1(ReadData), .out(multiplexer_2_out), .sel(lw));
  Multiplexer #(.width(32), .enable("false")) multiplexer_3 (
    .in0(multiplexer_2_out), .in1(bit_extender_1_out), .out(multiplexer_3_out), .sel(lbu));
  Multiplexer #(.width(32), .enable("false")) multiplexer_4 (
    .in0(multiplexer_3_out), .in1(bit_extender_4_out), .out(my_Output), .sel(lhu));
endmodule

module ControlLogic (
  input  [31:0] Instruction,
  input  BrEq,
  input  BrLt,
  output MemRW,
  output lh,
  output PCSel,
  output lw,
  output ASel,
  output RegWEn,
  output lbu,
  output BSel,
  output BrUn,
  output lhu,
  output [2:0] ImmSel,
  output lui,
  output [1:0] WBSel,
  output [3:0] ALUSel
);

  wire add, addi, addt, ALU, andi, andt, auipc, B, beq, beq_t, bgeu, bgeu_t, blt, blt_t, bltu, bltu_t, bne,
       bne_t, comparator_10_eq, comparator_11_eq, comparator_12_eq, comparator_13_eq, comparator_14_eq,
       comparator_15_eq, comparator_16_eq, comparator_17_eq, comparator_18_eq, comparator_19_eq,
       comparator_20_eq, comparator_21_eq, comparator_22_eq, comparator_23_eq, comparator_24_eq,
       comparator_25_eq, comparator_26_eq, comparator_27_eq, comparator_28_eq, comparator_29_eq,
       comparator_30_eq, comparator_31_eq, comparator_32_eq, comparator_33_eq, comparator_34_eq,
       comparator_35_eq, comparator_36_eq, comparator_37_eq, comparator_38_eq, comparator_39_eq,
       comparator_40_eq, comparator_41_eq, comparator_42_eq, comparator_43_eq, comparator_44_eq,
       comparator_45_eq, comparator_46_eq, comparator_47_eq, comparator_48_eq, comparator_49_eq,
       comparator_50_eq, comparator_51_eq, comparator_52_eq, comparator_53_eq, comparator_54_eq,
       comparator_55_eq, comparator_56_eq, comparator_57_eq, divu, I, Imm, Itype, J, lb, Load, mulh, mulhu,
       mult, my_and, my_or, my_sll, my_slt, my_sltu, my_sra, my_srl, my_xor, not_1_out, not_2_out, or_1_out,
       or_9_out, or_10_out, or_12_out, or_16_out, or_17_out, ori, ort, R, remu, S, slli, sllt, slti, sltt,
       srli, srlt, sub, xori, xort;
  wire [1:0] multiplexer_20_out, multiplexer_21_out;
  wire [2:0] multiplexer_8_out, multiplexer_11_out, multiplexer_13_out, multiplexer_15_out;
  wire [3:0] multiplexer_1_out, multiplexer_2_out, multiplexer_3_out, multiplexer_4_out, multiplexer_5_out,
       multiplexer_6_out, multiplexer_7_out, multiplexer_9_out, multiplexer_10_out, multiplexer_12_out,
       multiplexer_14_out, multiplexer_17_out, multiplexer_18_out;

  Multiplexer #(.width(4), .enable("false")) multiplexer_1 (
    .in0(4'b0000), .in1(4'b0001), .out(multiplexer_1_out), .sel(ort));
  not not_1 (not_1_out, BrEq);
  not not_2 (not_2_out, BrLt);
  Multiplexer #(.width(4), .enable("false")) multiplexer_2 (
    .in0(multiplexer_1_out), .in1(4'b0010), .out(multiplexer_2_out), .sel(xort));
  Comparator #(.width(7)) comparator_1 (.a(Instruction[6:0]), .b(7'b0110011), .eq(R));  // open: gt, lt
  Comparator #(.width(7)) comparator_2 (.a(Instruction[6:0]), .b(7'b0000011), .eq(Load));  // open: gt, lt
  Comparator #(.width(7)) comparator_3 (.a(Instruction[6:0]), .b(7'b0010011), .eq(Imm));  // open: gt, lt
  Comparator #(.width(7)) comparator_4 (.a(Instruction[6:0]), .b(7'b0100011), .eq(S));  // open: gt, lt
  Comparator #(.width(7)) comparator_5 (.a(Instruction[6:0]), .b(7'b1100011), .eq(B));  // open: gt, lt
  Comparator #(.width(7)) comparator_6 (.a(Instruction[6:0]), .b(7'b0110111), .eq(lui));  // open: gt, lt
  Comparator #(.width(7)) comparator_7 (.a(Instruction[6:0]), .b(7'b0010111), .eq(auipc));  // open: gt, lt
  Comparator #(.width(7)) comparator_8 (.a(Instruction[6:0]), .b(7'b1101111), .eq(J));  // open: gt, lt
  Comparator #(.width(7)) comparator_9 (.a(Instruction[6:0]), .b(7'b1100111), .eq(I));  // open: gt, lt
  and and_1 (bne_t, bne, not_1_out);
  and and_2 (beq_t, beq, BrEq);
  and and_3 (blt_t, blt, BrLt);
  and and_4 (bgeu_t, bgeu, not_2_out);
  and and_5 (bltu_t, bltu, BrLt);
  Multiplexer #(.width(4), .enable("false")) multiplexer_3 (
    .in0(multiplexer_2_out), .in1(4'b0011), .out(multiplexer_3_out), .sel(addt));
  not not_3 (RegWEn, or_1_out);
  or or_1 (or_1_out, beq, bne, blt, MemRW, bgeu, bltu);
  Multiplexer #(.width(4), .enable("false")) multiplexer_4 (
    .in0(multiplexer_3_out), .in1(4'b0100), .out(multiplexer_4_out), .sel(sub));
  Multiplexer #(.width(4), .enable("false")) multiplexer_5 (
    .in0(multiplexer_4_out), .in1(4'b0101), .out(multiplexer_5_out), .sel(mult));
  Multiplexer #(.width(4), .enable("false")) multiplexer_6 (
    .in0(multiplexer_5_out), .in1(4'b0110), .out(multiplexer_6_out), .sel(mulhu));
  Comparator #(.width(3), .mode("unsigned")) comparator_10 (
    .a(Instruction[14:12]), .b(3'b000), .eq(comparator_10_eq));  // open: gt, lt
  Comparator #(.width(7), .mode("unsigned")) comparator_11 (
    .a(Instruction[31:25]), .b({7{1'b0}}), .eq(comparator_11_eq));  // open: gt, lt
  Comparator #(.width(3), .mode("unsigned")) comparator_12 (
    .a(Instruction[14:12]), .b(3'b000), .eq(comparator_12_eq));  // open: gt, lt
  Comparator #(.width(7), .mode("unsigned")) comparator_13 (
    .a(Instruction[31:25]), .b(7'b0100000), .eq(comparator_13_eq));  // open: gt, lt
  Comparator #(.width(3), .mode("unsigned")) comparator_14 (
    .a(Instruction[14:12]), .b(3'b000), .eq(comparator_14_eq));  // open: gt, lt
  Comparator #(.width(7), .mode("unsigned")) comparator_15 (
    .a(Instruction[31:25]), .b(7'b0000001), .eq(comparator_15_eq));  // open: gt, lt
  Comparator #(.width(3), .mode("unsigned")) comparator_16 (
    .a(Instruction[14:12]), .b(3'b011), .eq(comparator_16_eq));  // open: gt, lt
  Comparator #(.width(7), .mode("unsigned")) comparator_17 (
    .a(Instruction[31:25]), .b(7'b0000001), .eq(comparator_17_eq));  // open: gt, lt
  Comparator #(.width(3), .mode("unsigned")) comparator_18 (
    .a(Instruction[14:12]), .b(3'b101), .eq(comparator_18_eq));  // open: gt, lt
  Comparator #(.width(7), .mode("unsigned")) comparator_19 (
    .a(Instruction[31:25]), .b(7'b0000001), .eq(comparator_19_eq));  // open: gt, lt
  Comparator #(.width(3), .mode("unsigned")) comparator_20 (
    .a(Instruction[14:12]), .b(3'b111), .eq(comparator_20_eq));  // open: gt, lt
  Comparator #(.width(7), .mode("unsigned")) comparator_21 (
    .a(Instruction[31:25]), .b(7'b0000001), .eq(comparator_21_eq));  // open: gt, lt
  or or_2 (andt, my_and, andi);
  or or_3 (ort, my_or, ori);
  or or_4 (xort, my_xor, xori);
  or or_5 (sltt, my_sltu, slti);
  or or_6 (srlt, my_srl, srli);
  or or_7 (sllt, my_sll, slli);
  Multiplexer #(.width(4), .enable("false")) multiplexer_7 (
    .in0(multiplexer_6_out), .in1(4'b0111), .out(multiplexer_7_out), .sel(mulh));
  and and_6 (add, comparator_10_eq, R, comparator_11_eq);
  and and_7 (sub, comparator_12_eq, R, comparator_13_eq);
  and and_8 (mult, comparator_14_eq, R, comparator_15_eq);
  and and_9 (mulhu, comparator_16_eq, R, comparator_17_eq);
  and and_10 (divu, comparator_18_eq, R, comparator_19_eq);
  and and_11 (remu, comparator_20_eq, R, comparator_21_eq);
  Multiplexer #(.width(3), .enable("false")) multiplexer_8 (
    .in0(3'b000), .in1(3'b000), .out(multiplexer_8_out), .sel(Itype));
  Multiplexer #(.width(4), .enable("false")) multiplexer_9 (
    .in0(multiplexer_7_out), .in1(4'b1000), .out(multiplexer_9_out), .sel(divu));
  Multiplexer #(.width(4), .enable("false")) multiplexer_10 (
    .in0(multiplexer_9_out), .in1(4'b1001), .out(multiplexer_10_out), .sel(remu));
  or or_8 (ALU, Imm, R, or_9_out);
  or or_9 (or_9_out, lui, auipc);
  Multiplexer #(.width(3), .enable("false")) multiplexer_11 (
    .in0(multiplexer_8_out), .in1(3'b001), .out(multiplexer_11_out), .sel(S));
  Multiplexer #(.width(4), .enable("false")) multiplexer_12 (
    .in0(multiplexer_10_out), .in1(4'b1010), .out(multiplexer_12_out), .sel(srlt));
  or or_10 (or_10_out, lui, auipc);
  Multiplexer #(.width(3), .enable("false")) multiplexer_13 (
    .in0(multiplexer_11_out), .in1(3'b010), .out(multiplexer_13_out), .sel(B));
  Multiplexer #(.width(4), .enable("false")) multiplexer_14 (
    .in0(multiplexer_12_out), .in1(4'b1011), .out(multiplexer_14_out), .sel(my_sra));
  Comparator #(.width(3), .mode("unsigned")) comparator_22 (
    .a(Instruction[14:12]), .b(3'b001), .eq(comparator_22_eq));  // open: gt, lt
  Comparator #(.width(7), .mode("unsigned")) comparator_23 (
    .a(Instruction[31:25]), .b({7{1'b0}}), .eq(comparator_23_eq));  // open: gt, lt
  Comparator #(.width(3), .mode("unsigned")) comparator_24 (
    .a(Instruction[14:12]), .b(3'b100), .eq(comparator_24_eq));  // open: gt, lt
  Comparator #(.width(7), .mode("unsigned")) comparator_25 (
    .a(Instruction[31:25]), .b({7{1'b0}}), .eq(comparator_25_eq));  // open: gt, lt
  Comparator #(.width(3), .mode("unsigned")) comparator_26 (
    .a(Instruction[14:12]), .b(3'b011), .eq(comparator_26_eq));  // open: gt, lt
  Comparator #(.width(7), .mode("unsigned")) comparator_27 (
    .a(Instruction[31:25]), .b({7{1'b0}}), .eq(comparator_27_eq));  // open: gt, lt
  Comparator #(.width(3), .mode("unsigned")) comparator_28 (
    .a(Instruction[14:12]), .b(3'b101), .eq(comparator_28_eq));  // open: gt, lt
  Comparator #(.width(7), .mode("unsigned")) comparator_29 (
    .a(Instruction[31:25]), .b({7{1'b0}}), .eq(comparator_29_eq));  // open: gt, lt
  Comparator #(.width(3), .mode("unsigned")) comparator_30 (
    .a(Instruction[14:12]), .b(3'b110), .eq(comparator_30_eq));  // open: gt, lt
  Comparator #(.width(7), .mode("unsigned")) comparator_31 (
    .a(Instruction[31:25]), .b({7{1'b0}}), .eq(comparator_31_eq));  // open: gt, lt
  Comparator #(.width(3), .mode("unsigned")) comparator_32 (
    .a(Instruction[14:12]), .b(3'b111), .eq(comparator_32_eq));  // open: gt, lt
  Comparator #(.width(7), .mode("unsigned")) comparator_33 (
    .a(Instruction[31:25]), .b({7{1'b0}}), .eq(comparator_33_eq));  // open: gt, lt
  or or_11 (addt, add, addi, or_10_out, B, J, I);
  Multiplexer #(.width(3), .enable("false")) multiplexer_15 (
    .in0(multiplexer_13_out), .in1(3'b011), .out(multiplexer_15_out), .sel(J));
  Multiplexer #(.width(3), .enable("false")) multiplexer_16 (
    .in0(multiplexer_15_out), .in1(3'b100), .out(ImmSel), .sel(or_12_out));
  or or_12 (or_12_out, lui, auipc);
  Multiplexer #(.width(4), .enable("false")) multiplexer_17 (
    .in0(multiplexer_14_out), .in1(4'b1100), .out(multiplexer_17_out), .sel(sllt));
  Multiplexer #(.width(4), .enable("false")) multiplexer_18 (
    .in0(multiplexer_17_out), .in1(4'b1101), .out(multiplexer_18_out), .sel(sltt));
  and and_12 (my_sll, comparator_22_eq, R, comparator_23_eq);
  and and_13 (my_xor, comparator_24_eq, R, comparator_25_eq);
  and and_14 (my_sltu, comparator_26_eq, R, comparator_27_eq);
  and and_15 (my_srl, comparator_28_eq, R, comparator_29_eq);
  and and_16 (my_or, comparator_30_eq, R, comparator_31_eq);
  and and_17 (my_and, comparator_32_eq, R, comparator_33_eq);
  Multiplexer #(.width(4), .enable("false")) multiplexer_19 (
    .in0(multiplexer_18_out), .in1(4'b1110), .out(ALUSel), .sel(my_slt));
  or or_13 (Itype, Load, I, Imm);
  not not_4 (BSel, R);
  Multiplexer #(.width(2), .enable("false")) multiplexer_20 (
    .in0(2'b00), .in1(2'b00), .out(multiplexer_20_out), .sel(Load));
  or or_14 (ASel, beq, bne, blt, bltu, bgeu, J, auipc);
  or or_15 (PCSel, beq_t, bne_t, blt_t, bgeu_t, bltu_t, J, I);
  Multiplexer #(.width(2), .enable("false")) multiplexer_21 (
    .in0(multiplexer_20_out), .in1(2'b01), .out(multiplexer_21_out), .sel(ALU));
  Comparator #(.width(3), .mode("unsigned")) comparator_34 (
    .a(Instruction[14:12]), .b(3'b001), .eq(comparator_34_eq));  // open: gt, lt
  Comparator #(.width(3), .mode("unsigned")) comparator_35 (
    .a(Instruction[14:12]), .b(3'b010), .eq(comparator_35_eq));  // open: gt, lt
  Comparator #(.width(3), .mode("unsigned")) comparator_36 (
    .a(Instruction[14:12]), .b(3'b000), .eq(comparator_36_eq));  // open: gt, lt
  Comparator #(.width(3), .mode("unsigned")) comparator_37 (
    .a(Instruction[14:12]), .b(3'b100), .eq(comparator_37_eq));  // open: gt, lt
  Comparator #(.width(3), .mode("unsigned")) comparator_38 (
    .a(Instruction[14:12]), .b(3'b101), .eq(comparator_38_eq));  // open: gt, lt
  Comparator #(.width(3), .mode("unsigned")) comparator_39 (
    .a(Instruction[14:12]), .b(3'b001), .eq(comparator_39_eq));  // open: gt, lt
  Comparator #(.width(7), .mode("unsigned")) comparator_40 (
    .a(Instruction[31:25]), .b(7'b0000001), .eq(comparator_40_eq));  // open: gt, lt
  Multiplexer #(.width(2), .enable("false")) multiplexer_22 (
    .in0(multiplexer_21_out), .in1(2'b10), .out(WBSel), .sel(or_16_out));
  or or_16 (or_16_out, I, J);
  and and_18 (lh, comparator_34_eq, Load);
  and and_19 (lw, comparator_35_eq, Load);
  and and_20 (lb, comparator_36_eq, Load);
  and and_21 (lbu, comparator_37_eq, Load);
  and and_22 (lhu, comparator_38_eq, Load);
  and and_23 (mulh, comparator_39_eq, R, comparator_40_eq);
  Comparator #(.width(3), .mode("unsigned")) comparator_41 (
    .a(Instruction[14:12]), .b(3'b010), .eq(comparator_41_eq));  // open: gt, lt
  Comparator #(.width(7), .mode("unsigned")) comparator_42 (
    .a(Instruction[31:25]), .b({7{1'b0}}), .eq(comparator_42_eq));  // open: gt, lt
  and and_24 (my_slt, comparator_41_eq, R, comparator_42_eq);
  Comparator #(.width(3), .mode("unsigned")) comparator_43 (
    .a(Instruction[14:12]), .b(3'b010), .eq(comparator_43_eq));  // open: gt, lt
  Comparator #(.width(3), .mode("unsigned")) comparator_44 (
    .a(Instruction[14:12]), .b(3'b100), .eq(comparator_44_eq));  // open: gt, lt
  Comparator #(.width(3), .mode("unsigned")) comparator_45 (
    .a(Instruction[14:12]), .b(3'b101), .eq(comparator_45_eq));  // open: gt, lt
  Comparator #(.width(7), .mode("unsigned")) comparator_46 (
    .a(Instruction[31:25]), .b(7'b0100000), .eq(comparator_46_eq));  // open: gt, lt
  Comparator #(.width(3), .mode("unsigned")) comparator_47 (
    .a(Instruction[14:12]), .b(3'b110), .eq(comparator_47_eq));  // open: gt, lt
  Comparator #(.width(3), .mode("unsigned")) comparator_48 (
    .a(Instruction[14:12]), .b(3'b111), .eq(comparator_48_eq));  // open: gt, lt
  Comparator #(.width(3), .mode("unsigned")) comparator_49 (
    .a(Instruction[14:12]), .b(3'b101), .eq(comparator_49_eq));  // open: gt, lt
  and and_25 (slti, comparator_43_eq, Imm);
  and and_26 (xori, comparator_44_eq, Imm);
  and and_27 (srli, comparator_49_eq, Imm);
  and and_28 (my_sra, comparator_45_eq, R, comparator_46_eq);
  and and_29 (ori, comparator_47_eq, Imm);
  and and_30 (andi, comparator_48_eq, Imm);
  Comparator #(.width(3), .mode("unsigned")) comparator_50 (
    .a(Instruction[14:12]), .b(3'b000), .eq(comparator_50_eq));  // open: gt, lt
  Comparator #(.width(3), .mode("unsigned")) comparator_51 (
    .a(Instruction[14:12]), .b(3'b001), .eq(comparator_51_eq));  // open: gt, lt
  Comparator #(.width(3), .mode("unsigned")) comparator_52 (
    .a(Instruction[14:12]), .b(3'b010), .eq(comparator_52_eq));  // open: gt, lt
  Comparator #(.width(3), .mode("unsigned")) comparator_53 (
    .a(Instruction[14:12]), .b(3'b000), .eq(comparator_53_eq));  // open: gt, lt
  Comparator #(.width(3), .mode("unsigned")) comparator_54 (
    .a(Instruction[14:12]), .b(3'b100), .eq(comparator_54_eq));  // open: gt, lt
  Comparator #(.width(3), .mode("unsigned")) comparator_55 (
    .a(Instruction[14:12]), .b(3'b110), .eq(comparator_55_eq));  // open: gt, lt
  and and_31 (addi, comparator_50_eq, Imm);
  and and_32 (slli, comparator_51_eq, Imm);
  and and_33 (MemRW, comparator_52_eq, S);
  and and_34 (beq, comparator_53_eq, B);
  and and_35 (blt, comparator_54_eq, B);
  and and_36 (bltu, comparator_55_eq, B);
  Comparator #(.width(3), .mode("unsigned")) comparator_56 (
    .a(Instruction[14:12]), .b(3'b001), .eq(comparator_56_eq));  // open: gt, lt
  Comparator #(.width(3), .mode("unsigned")) comparator_57 (
    .a(Instruction[14:12]), .b(3'b111), .eq(comparator_57_eq));  // open: gt, lt
  or or_17 (or_17_out, bltu, bgeu);
  and and_37 (bne, comparator_56_eq, B);
  and and_38 (bgeu, comparator_57_eq, B);
  and and_39 (BrUn, or_17_out, B);

  // Other names for the same wires on the sheet: opcode[6:0] = Instruction[6:0]; func3[2:0] = Instruction[14:12];
  //   func7[6:0] = Instruction[31:25]; jal = J; jalr = I; sw = MemRW
endmodule
